// Logisim project Assignment 1-Anirudh.circ as structural Verilog: 1 circuit, main circuit main
module main (
  input  A,
  input  B,
  input  C
);

  wire and_1_out, and_2_out, and_3_out, and_4_out, and_5_out, not_1_out, not_2_out, not_3_out, or_1_out,
       or_2_out, xor_1_out;

  and and_1 (and_1_out, not_3_out, B);
  and and_2 (and_2_out, C, not_2_out);
  not not_1 (not_1_out, A);
  not not_2 (not_2_out, B);
  not not_3 (not_3_out, C);
  or or_1 (or_1_out, and_1_out, and_2_out);
  and and_3 (and_3_out, C, B);
  and and_4 (and_4_out, not_1_out, not_2_out, not_3_out);
  ExactlyOne xor_1 (.out(xor_1_out), .in1(C), .in2(B), .in3(A));
  and and_5 (and_5_out, or_1_out, A);
  or or_2 (or_2_out, and_5_out, and_3_out);
  LED led_1 (.in(or_2_out));
  LED led_2 (.in(xor_1_out));
  LED led_3 (.in(and_4_out));
endmodule
